// Logisim project MOTO.circ as structural Verilog: 6 circuits, main circuit PROCESSADOR
module PROCESSADOR (
  output [31:0] \INSTRUÇÃO 
);

  wire and_1_out, bg1, bge, brch, brchS, brchS1, CLK, ime, imeS, j, jS, jS1, or_1_out, redm, redmS, redmS1,
       redmS2, register_11_q, RESET, wm, wmS, wmS1, wr, wrs, wrs1, wrs2;
  wire [3:0] op, opS, R3, R4, register_2_q, RX;
  wire [4:0] shamtR;
  wire [7:0] multiplexer_4_out, PC_q_2;
  wire [15:0] ADJU;
  wire [31:0] adder_1_out, ADJU1, ADJU2, bit_extender_1_out, DATA_W, memoria_de_dados_1_out_7,
       multiplexer_1_out, PC_q, reg0, reg0S, reg0S1, reg1, reg1S, register_12_q, register_13_q, rom_1_data,
       ulaR, ulaR1, ulaR2;

  Adder #(.width(32)) adder_1 (.a({PC_q[31:10], PC_q_2, PC_q[1:0]}), .b(32'h4), .out(adder_1_out));  // open: cin, cout
  Multiplexer #(.width(32), .enable("false")) multiplexer_1 (
    .in0(adder_1_out), .in1(ADJU2), .out(multiplexer_1_out), .sel(or_1_out));
  or or_1 (or_1_out, jS1, and_1_out);
  and and_1 (and_1_out, brchS1, bg1);
  Register #(.width(32)) PC (
    .D(multiplexer_1_out), .Q({PC_q[31:10], PC_q_2, PC_q[1:0]}), .clk(CLK), .clr(RESET));  // open: en
  Clock clock_1 (.out(CLK));
  Button button_1 (.out(RESET));
  ROM #(.dataWidth(32)) rom_1 (.addr(PC_q_2), .data(rom_1_data));  // open: sel
  Register #(.width(32)) register_1 (.D(rom_1_data), .Q(\INSTRUÇÃO ), .clk(CLK), .clr(RESET));  // open: en
  UC uc_1 (
    .E0(\INSTRUÇÃO [31]), .E1(\INSTRUÇÃO [30]), .E2(\INSTRUÇÃO [29]), .write_reg(wr), .E3(\INSTRUÇÃO [28]),
    .branch(brch), .read_mem(redm), .write_mem(wm), .jump(j), .imediato(ime), .out_11(op));
  Register #(.width(4)) register_2 (.D(\INSTRUÇÃO [27:24]), .Q(register_2_q), .clk(CLK), .clr(RESET));  // open: en
  Register #(.width(4)) register_3 (.D(register_2_q), .Q(R3), .clk(CLK), .clr(RESET));  // open: en
  Banco_Registradores banco_registradores_1 (
    .DATA_WRITE(DATA_W), .RW(R4), .R0_D(reg0), .R0(\INSTRUÇÃO [19:16]), .R1_D(reg1), .R1(\INSTRUÇÃO [23:20]),
    .\operação (wrs2), .clock(CLK), .reset(RESET));
  pipeline pipeline_1 (
    .write_reg(wr), .branch(brch), .read_mem(redm), .jump(j), .write_mem(wm), .imediato(ime), .opcode(op),
    .REG0_D(reg0), .REG1_D(reg1), .write_reg_S(wrs), .branch_S(brchS), .read_mem_S(redmS), .jump_S(jS),
    .write_mem_S(wmS), .imediato_S(imeS), .opcode_S(opS), .REGO_S(reg0S), .REG1__S(reg1S), .clock(CLK),
    .reset(RESET), .shamt(\INSTRUÇÃO [4:0]), .\endereço_jump (\INSTRUÇÃO [15:0]), .out_23(shamtR),
    .out_24(ADJU));
  Multiplexer #(.width(32), .enable("false")) multiplexer_2 (
    .in0(ulaR2), .in1(register_13_q), .out(DATA_W), .sel(redmS2));
  Ula ula_1 (.A(reg0S), .B(reg1S), .ULA_OP(opS), .SHAMT(shamtR), .bge(bge), .ula_resposta(ulaR));
  Multiplexer #(.width(4), .enable("false")) multiplexer_3 (.in0(R3), .in1(R4), .out(RX), .sel(redmS2));
  assign bit_extender_1_out = {{16{1'b0}}, ADJU};  // Bit_Extender bit_extender_1
  Register #(.width(32)) register_4 (.D(reg0S), .Q(reg0S1), .clk(CLK), .clr(RESET));  // open: en
  Register #(.width(32)) register_5 (.D(ulaR), .Q(ulaR1), .clk(CLK), .clr(RESET));  // open: en
  Register #(.width(1)) register_6 (.D(wmS), .Q(wmS1), .clk(CLK), .clr(RESET));  // open: en
  Register #(.width(1)) register_7 (.D(redmS), .Q(redmS1), .clk(CLK), .clr(RESET));  // open: en
  Register #(.width(4)) register_8 (.D(R3), .Q(R4), .clk(CLK), .clr(RESET));  // open: en
  Register #(.width(1)) register_9 (.D(wrs), .Q(wrs1), .clk(CLK), .clr(RESET));  // open: en
  Register #(.width(32)) register_10 (.D(bit_extender_1_out), .Q(ADJU1), .clk(CLK), .clr(RESET));  // open: en
  Multiplexer #(.width(8), .enable("false")) multiplexer_4 (
    .in0(reg0S1[7:0]), .in1(ulaR1[7:0]), .out(multiplexer_4_out), .sel(redmS1));
  memoria_de_dados memoria_de_dados_1 (
    .Adress(multiplexer_4_out), .LW(redmS1), .SW(wmS1), .in_6(ulaR1), .CLK(CLK), .RESET(RESET),
    .out_7(memoria_de_dados_1_out_7));
  Register #(.width(1)) register_11 (.D(wrs1), .Q(register_11_q), .clk(CLK), .clr(RESET));  // open: en
  Register #(.width(32)) register_12 (.D(ADJU1), .Q(register_12_q), .clk(CLK), .clr(RESET));  // open: en
  Register #(.width(32)) register_13 (
    .D(memoria_de_dados_1_out_7), .Q(register_13_q), .clk(CLK), .clr(RESET));  // open: en
  Register #(.width(1)) register_14 (.D(redmS1), .Q(redmS2), .clk(CLK), .clr(RESET));  // open: en
  Register #(.width(32)) register_15 (.D(ulaR1), .Q(ulaR2), .clk(CLK), .clr(RESET));  // open: en
  Register #(.width(1)) register_16 (.D(bge), .Q(bg1), .clk(CLK), .clr(RESET));  // open: en
  Register #(.width(1)) register_17 (.D(jS), .Q(jS1), .clk(CLK), .clr(RESET));  // open: en
  Register #(.width(1)) register_18 (.D(brchS), .Q(brchS1), .clk(CLK), .clr(RESET));  // open: en
  Register #(.width(1)) register_19 (.D(register_11_q), .Q(wrs2), .clk(CLK), .clr(RESET));  // open: en
  Register #(.width(32)) register_20 (.D(register_12_q), .Q(ADJU2), .clk(CLK), .clr(RESET));  // open: en

  // Notes on the sheet:
  //   contents of rom_1 (hex, n*v repeats v):
  //   4*7f000000 70000000 4*7f000000 7d000004 4*7f000000 7c000008 4*7f000000 70000000 4*7f000000 71000000
  //   4*7f000000 72000000 4*7f000000 7b000002 4*7f000000 600b00b4 4*7f000000 71000000 4*7f000000 601b02e8
  //   4*7f000000 72000000 4*7f000000 73000000 4*7f000000 240b0000 4*7f000000 4410000 4*7f000000 44c0000
  //   5*7f000000 80f40000 5*7f000000 602b02a0 5*7f000000 260b0000 5*7f000000 6620000 5*7f000000 66e0000
  //   5*7f000000 95a60000 7*7f000000 272b0000 7*7f000000 7710000 7*7f000000 98d70000 5*7f000000 29580000
  //   7*7f000000 3390000 7*7f000000 32020001 7*7f000000 50000040 5*7f000000 80340000 8*7f000000 31010001
  //   10*7f000000 500000d8 5*7f000000 30000001 7*7f000000 500000a8 7*7f000000 50000318 7f000000 7f000000
  //   7f000000
  //   REG_W
  //   UC
  //   REG_0
  //   REG_1
  //   banco registradores
  //   REG0_D
  //   REG1_D
  //   ULA
  //   SW
  //   LW
  //   memória de dados
endmodule

module Ula (
  input  [31:0] A,
  input  [31:0] B,
  input  [3:0] ULA_OP,
  input  [4:0] SHAMT,
  output [31:0] ula_resposta,
  output bge
);

  wire comparator_1_eq, comparator_1_lt;
  wire [31:0] adder_1_out, adder_2_out, bit_extender_1_out, multiplier_1_out, subtractor_1_out;

  assign bit_extender_1_out = {{27{1'b0}}, SHAMT};  // Bit_Extender bit_extender_1
  Adder #(.width(32)) adder_1 (.a(A), .b(B), .out(adder_1_out));  // open: cin, cout
  Subtractor #(.width(32)) subtractor_1 (.a(B), .b(A), .out(subtractor_1_out));  // open: bin, bout
  Multiplier #(.width(32)) multiplier_1 (.a(A), .b(B), .out(multiplier_1_out));  // open: cin, cout
  Comparator #(.width(32), .mode("unsigned")) comparator_1 (
    .a(A), .b(B), .eq(comparator_1_eq), .lt(comparator_1_lt));  // open: gt
  Adder #(.width(32)) adder_2 (.a(A), .b(bit_extender_1_out), .out(adder_2_out));  // open: cin, cout
  or or_1 (bge, comparator_1_eq, comparator_1_lt);
  Multiplexer #(.select(4), .width(32), .enable("false")) multiplexer_1 (
    .in0(adder_1_out), .in1(subtractor_1_out), .in2(multiplier_1_out), .in3(adder_2_out),
    .in7(bit_extender_1_out), .in8(B), .in9(adder_1_out), .out(ula_resposta), .sel(ULA_OP));  // open: in4, in5, in6, in10, in11, in12, in13, in14, in15
endmodule

module Banco_Registradores (
  input  [31:0] DATA_WRITE,
  input  [3:0] R0,
  input  [3:0] R1,
  input  [3:0] RW,
  input  clock,
  input  reset,
  input  \operação ,
  output [31:0] R0_D,
  output [31:0] R1_D
);

  wire demultiplexer_1_out0, demultiplexer_1_out1, demultiplexer_1_out2, demultiplexer_1_out3,
       demultiplexer_1_out4, demultiplexer_1_out5, demultiplexer_1_out6, demultiplexer_1_out7,
       demultiplexer_1_out8, demultiplexer_1_out9, demultiplexer_1_out10, demultiplexer_1_out11,
       demultiplexer_1_out12, demultiplexer_1_out13, demultiplexer_1_out14, demultiplexer_1_out15;
  wire [31:0] _2_q, register_1_q, register_2_q, register_3_q, register_4_q, register_5_q, register_6_q,
       register_7_q, register_8_q, register_9_q, register_10_q, register_11_q, register_12_q, register_13_q,
       register_14_q, register_15_q;

  Demultiplexer #(.select(4), .enable("false")) demultiplexer_1 (
    .out0(demultiplexer_1_out0), .out1(demultiplexer_1_out1), .out2(demultiplexer_1_out2),
    .out3(demultiplexer_1_out3), .out4(demultiplexer_1_out4), .out5(demultiplexer_1_out5),
    .out6(demultiplexer_1_out6), .out7(demultiplexer_1_out7), .out8(demultiplexer_1_out8),
    .out9(demultiplexer_1_out9), .out10(demultiplexer_1_out10), .out11(demultiplexer_1_out11),
    .out12(demultiplexer_1_out12), .out13(demultiplexer_1_out13), .out14(demultiplexer_1_out14),
    .out15(demultiplexer_1_out15), .in(\operação ), .sel(RW));
  Register #(.width(32)) register_1 (
    .D(DATA_WRITE), .en(demultiplexer_1_out0), .Q(register_1_q), .clk(clock), .clr(reset));
  Register #(.width(32)) register_2 (
    .D(DATA_WRITE), .en(demultiplexer_1_out1), .Q(register_2_q), .clk(clock), .clr(reset));
  Register #(.width(32)) _2 (.D(DATA_WRITE), .en(demultiplexer_1_out2), .Q(_2_q), .clk(clock), .clr(reset));
  Register #(.width(32)) register_3 (
    .D(DATA_WRITE), .en(demultiplexer_1_out3), .Q(register_3_q), .clk(clock), .clr(reset));
  Register #(.width(32)) register_4 (
    .D(DATA_WRITE), .en(demultiplexer_1_out4), .Q(register_4_q), .clk(clock), .clr(reset));
  Register #(.width(32)) register_5 (
    .D(DATA_WRITE), .en(demultiplexer_1_out5), .Q(register_5_q), .clk(clock), .clr(reset));
  Register #(.width(32)) register_6 (
    .D(DATA_WRITE), .en(demultiplexer_1_out6), .Q(register_6_q), .clk(clock), .clr(reset));
  Register #(.width(32)) register_7 (
    .D(DATA_WRITE), .en(demultiplexer_1_out7), .Q(register_7_q), .clk(clock), .clr(reset));
  Register #(.width(32)) register_8 (
    .D(DATA_WRITE), .en(demultiplexer_1_out8), .Q(register_8_q), .clk(clock), .clr(reset));
  Register #(.width(32)) register_9 (
    .D(DATA_WRITE), .en(demultiplexer_1_out9), .Q(register_9_q), .clk(clock), .clr(reset));
  Register #(.width(32)) register_10 (
    .D(DATA_WRITE), .en(demultiplexer_1_out10), .Q(register_10_q), .clk(clock), .clr(reset));
  Register #(.width(32)) register_11 (
    .D(DATA_WRITE), .en(demultiplexer_1_out11), .Q(register_11_q), .clk(clock), .clr(reset));
  Register #(.width(32)) register_12 (
    .D(DATA_WRITE), .en(demultiplexer_1_out12), .Q(register_12_q), .clk(clock), .clr(reset));
  Register #(.width(32)) register_13 (
    .D(DATA_WRITE), .en(demultiplexer_1_out13), .Q(register_13_q), .clk(clock), .clr(reset));
  Register #(.width(32)) register_14 (
    .D(DATA_WRITE), .en(demultiplexer_1_out14), .Q(register_14_q), .clk(clock), .clr(reset));
  Register #(.width(32)) register_15 (
    .en(demultiplexer_1_out15), .Q(register_15_q), .clk(clock), .clr(reset));  // open: D
  Multiplexer #(.select(4), .width(32), .enable("false")) multiplexer_1 (
    .in0(register_1_q), .in1(register_2_q), .in2(_2_q), .in3(register_3_q), .in4(register_4_q),
    .in5(register_5_q), .in6(register_6_q), .in7(register_7_q), .in8(register_8_q), .in9(register_9_q),
    .in10(register_10_q), .in11(register_11_q), .in12(register_12_q), .in13(register_13_q),
    .in14(register_14_q), .in15(register_15_q), .out(R0_D), .sel(R0));
  Multiplexer #(.select(4), .width(32), .enable("false")) multiplexer_2 (
    .in0(register_1_q), .in1(register_2_q), .in2(_2_q), .in3(register_3_q), .in4(register_4_q),
    .in5(register_5_q), .in6(register_6_q), .in7(register_7_q), .in8(register_8_q), .in9(register_9_q),
    .in10(register_10_q), .in11(register_11_q), .in12(register_12_q), .in13(register_13_q),
    .in14(register_14_q), .in15(register_15_q), .out(R1_D), .sel(R1));

  // Notes on the sheet:
  //   0
  //   1
  //   2
  //   3
  //   4
  //   5
  //   6
  //   7
  //   8
  //   9
  //   A
  //   B
  //   C
  //   DD
  //   E
  //   F
endmodule

module UC (
  input  E0,
  input  E1,
  input  E2,
  input  E3,
  output write_reg,
  output branch,
  output read_mem,
  output write_mem,
  output jump,
  output imediato,
  output [3:0] out_11
);

  wire and_1_out, and_2_out, and_3_out, and_4_out, and_5_out, and_6_out, and_8_out, and_9_out, and_11_out,
       and_12_out, not_1_out, not_2_out, not_3_out, not_4_out, not_5_out, not_6_out, not_7_out, not_8_out,
       not_9_out, not_10_out, not_11_out, not_12_out, not_13_out, not_14_out, uiui;

  not not_1 (not_1_out, E0);
  and and_1 (and_1_out, not_1_out, not_2_out);
  not not_2 (not_2_out, E1);
  not not_3 (not_3_out, E0);
  and and_2 (and_2_out, not_3_out, not_4_out, not_5_out);
  not not_4 (not_4_out, E2);
  not not_5 (not_5_out, E3);
  not not_6 (not_6_out, E1);
  and and_3 (and_3_out, not_6_out, E3);
  and and_4 (and_4_out, E2, E3);
  and and_5 (and_5_out, E1, E2, not_7_out);
  not not_7 (not_7_out, E3);
  and and_6 (and_6_out, E0, E1);
  and and_7 (read_mem, E0, E3);
  and and_8 (and_8_out, E0, not_8_out);
  not not_8 (not_8_out, E3);
  and and_9 (and_9_out, E0, E1);
  not not_9 (not_9_out, E2);
  and and_10 (jump, E1, not_9_out, E3);
  and and_11 (and_11_out, E2, E3);
  and and_12 (and_12_out, E1, not_10_out, not_11_out);
  not not_10 (not_10_out, E2);
  not not_11 (not_11_out, E3);
  or or_1 (write_reg, and_1_out, and_2_out, and_3_out, and_4_out);
  or or_2 (branch, and_5_out, and_6_out);
  or or_3 (write_mem, and_8_out, and_9_out);
  or or_4 (imediato, and_11_out, and_12_out);
  not not_12 (not_12_out, E0);
  not not_13 (not_13_out, E2);
  not not_14 (not_14_out, E3);
  and and_13 (uiui, not_12_out, E1, not_13_out, not_14_out);

  assign out_11 = {E0, E1, E2, E3};

  // Other names for the same wires on the sheet: _3 = E3; _2 = E2; _1 = E1; _0 = E0
endmodule

module memoria_de_dados (
  input  [7:0] Adress,
  input  LW,
  input  CLK,
  input  RESET,
  input  SW,
  input  [31:0] in_6,
  output [31:0] out_7
);

  RAM #(.dataWidth(32), .bus("separate")) ram_1 (
    .addr(Adress), .din(in_6), .data(out_7), .str(SW), .clk(CLK), .ld(LW), .clr(RESET));  // open: sel
endmodule

module pipeline (
  input  write_reg,
  input  branch,
  input  read_mem,
  input  jump,
  input  write_mem,
  input  imediato,
  input  [3:0] opcode,
  input  [31:0] REG0_D,
  input  [31:0] REG1_D,
  input  [4:0] shamt,
  input  [15:0] \endereço_jump ,
  input  clock,
  input  reset,
  output write_reg_S,
  output branch_S,
  output read_mem_S,
  output jump_S,
  output write_mem_S,
  output imediato_S,
  output [3:0] opcode_S,
  output [31:0] REGO_S,
  output [31:0] REG1__S,
  output [4:0] out_23,
  output [15:0] out_24
);

  Register #(.width(1)) register_1 (.D(write_reg), .Q(write_reg_S), .clk(clock), .clr(reset));  // open: en
  Register #(.width(1)) register_2 (.D(branch), .Q(branch_S), .clk(clock), .clr(reset));  // open: en
  Register #(.width(1)) register_3 (.D(read_mem), .Q(read_mem_S), .clk(clock), .clr(reset));  // open: en
  Register #(.width(1)) register_4 (.D(jump), .Q(jump_S), .clk(clock), .clr(reset));  // open: en
  Register #(.width(1)) register_5 (.D(write_mem), .Q(write_mem_S), .clk(clock), .clr(reset));  // open: en
  Register #(.width(1)) register_6 (.D(imediato), .Q(imediato_S), .clk(clock), .clr(reset));  // open: en
  Register #(.width(4)) register_7 (.D(opcode), .Q(opcode_S), .clk(clock), .clr(reset));  // open: en
  Register #(.width(32)) register_8 (.D(REG0_D), .Q(REGO_S), .clk(clock), .clr(reset));  // open: en
  Register #(.width(32)) register_9 (.D(REG1_D), .Q(REG1__S), .clk(clock), .clr(reset));  // open: en
  Register #(.width(5)) register_10 (.D(shamt), .Q(out_23), .clk(clock), .clr(reset));  // open: en
  Register #(.width(16)) register_11 (.D(\endereço_jump ), .Q(out_24), .clk(clock), .clr(reset));  // open: en

  // Other names for the same wires on the sheet: CLK = clock; RST = reset
endmodule
