// Logisim project microprocessadorMips.circ as structural Verilog: 5 circuits, main circuit PROCESSADOR
module PROCESSADOR (
  output [31:0] \INSTRUÇÃO 
);

  wire and_1_out, and_2_out, CLK, ime, LW, not_1_out, or_1_out, RESET, uc_1_branch, uc_1_jump,
       uc_1_write_mem, uc_1_write_reg, ula_1_out_6;
  wire [3:0] op;
  wire [7:0] multiplexer_4_out;
  wire [31:0] adder_1_out, banco_registradores_1_r0_d, banco_registradores_1_r1_d, bit_extender_1_out,
       bit_extender_2_out, memoria_de_dados_1_out_7, multiplexer_1_out, multiplexer_2_out, multiplexer_3_out,
       PC_q, ula_1_out_5;

  Adder #(.width(32)) adder_1 (.a(PC_q), .b(32'h4), .out(adder_1_out));  // open: cin, cout
  Multiplexer #(.width(32), .enable("false")) multiplexer_1 (
    .in0(adder_1_out), .in1(bit_extender_1_out), .out(multiplexer_1_out), .sel(or_1_out));
  or or_1 (or_1_out, and_1_out, and_2_out);
  and and_1 (and_1_out, uc_1_branch, ula_1_out_6);
  and and_2 (and_2_out, not_1_out, uc_1_jump);
  not not_1 (not_1_out, uc_1_branch);
  Register #(.width(32)) PC (.D(multiplexer_1_out), .Q(PC_q), .clk(CLK), .clr(RESET));  // open: en
  Clock clock_1 (.out(CLK));
  Button button_1 (.out(RESET));
  ROM #(.dataWidth(32)) rom_1 (.addr(PC_q[9:2]), .data(\INSTRUÇÃO ));  // open: sel
  UC uc_1 (
    .E0(\INSTRUÇÃO [31]), .E1(\INSTRUÇÃO [30]), .E2(\INSTRUÇÃO [29]), .write_reg(uc_1_write_reg),
    .E3(\INSTRUÇÃO [28]), .branch(uc_1_branch), .read_mem(LW), .write_mem(uc_1_write_mem), .jump(uc_1_jump),
    .imediato(ime), .out_11(op));
  Banco_Registradores banco_registradores_1 (
    .DATA_WRITE(multiplexer_3_out), .RW(\INSTRUÇÃO [27:24]), .R0_D(banco_registradores_1_r0_d),
    .R0(\INSTRUÇÃO [19:16]), .R1_D(banco_registradores_1_r1_d), .R1(\INSTRUÇÃO [23:20]),
    .\operação (uc_1_write_reg), .clock(CLK), .reset(RESET));
  assign bit_extender_1_out = {{16{1'b0}}, \INSTRUÇÃO [15:0]};  // Bit_Extender bit_extender_1
  assign bit_extender_2_out = {{16{1'b0}}, \INSTRUÇÃO [15:0]};  // Bit_Extender bit_extender_2
  Multiplexer #(.width(32), .enable("false")) multiplexer_2 (
    .in0(banco_registradores_1_r1_d), .in1(bit_extender_2_out), .out(multiplexer_2_out), .sel(ime));
  Ula ula_1 (
    .A(banco_registradores_1_r0_d), .B(multiplexer_2_out), .ULA_OP(op), .SHAMT(\INSTRUÇÃO [4:0]),
    .out_6(ula_1_out_6), .out_5(ula_1_out_5));
  Multiplexer #(.width(32), .enable("false")) multiplexer_3 (
    .in0(ula_1_out_5), .in1(memoria_de_dados_1_out_7), .out(multiplexer_3_out), .sel(LW));
  Multiplexer #(.width(8), .enable("false")) multiplexer_4 (
    .in0(banco_registradores_1_r0_d[7:0]), .in1(ula_1_out_5[7:0]), .out(multiplexer_4_out), .sel(LW));
  memoria_de_dados memoria_de_dados_1 (
    .Adress(multiplexer_4_out), .LW(LW), .SW(uc_1_write_mem), .in_4(ula_1_out_5), .CLK(CLK), .RESET(RESET),
    .out_7(memoria_de_dados_1_out_7));

  // Notes on the sheet:
  //   contents of rom_1 (hex, n*v repeats v):
  //   7e000000 7d000004 7c000008 70000000 71000000 72000000 7b000002 600b00b4 71000000 601b007c 72000000
  //   73000000 240b0000 4410000 44c0000 80f40000 602b0070 260b0000 6620000 66e0000 95a60000 272b0000
  //   7710000 98d70000 29580000 3390000 32020001 50000040 80340000 31010001 50000024 30000001 5000001c
  //   REG_0
  //   REG_1
  //   REG_W
  //   UC
  //   DATA_W
  //   banco registradores
  //   REG0_D
  //   REG1_D
  //   ULA
  //   memória de dados
endmodule

module Ula (
  input  [31:0] A,
  input  [31:0] B,
  input  [3:0] ULA_OP,
  input  [4:0] SHAMT,
  output [31:0] out_5,
  output out_6
);

  wire comparator_1_eq, comparator_1_lt;
  wire [31:0] adder_1_out, adder_2_out, bit_extender_1_out, multiplier_1_out, shifter_1_out, subtractor_1_out;

  assign bit_extender_1_out = {{27{1'b0}}, SHAMT};  // Bit_Extender bit_extender_1
  Adder #(.width(32)) adder_1 (.a(A), .b(B), .out(adder_1_out));  // open: cin, cout
  Subtractor #(.width(32)) subtractor_1 (.a(B), .b(A), .out(subtractor_1_out));  // open: bin, bout
  Multiplier #(.width(32)) multiplier_1 (.a(A), .b(B), .out(multiplier_1_out));  // open: cin, cout
  Comparator #(.width(32), .mode("unsigned")) comparator_1 (
    .a(A), .b(B), .eq(comparator_1_eq), .lt(comparator_1_lt));  // open: gt
  Shifter #(.width(32)) shifter_1 (.in(A), .\dist (SHAMT), .out(shifter_1_out));
  Adder #(.width(32)) adder_2 (.a(A), .b(bit_extender_1_out), .out(adder_2_out));  // open: cin, cout
  or or_1 (out_6, comparator_1_eq, comparator_1_lt);
  Multiplexer #(.select(4), .width(32), .enable("false")) multiplexer_1 (
    .in0(adder_1_out), .in1(subtractor_1_out), .in2(multiplier_1_out), .in3(adder_2_out),
    .in4(shifter_1_out), .in7(bit_extender_1_out), .in8(B), .in9(adder_1_out), .out(out_5), .sel(ULA_OP));  // open: in5, in6, in10, in11, in12, in13, in14, in15
endmodule

module Banco_Registradores (
  input  [31:0] DATA_WRITE,
  input  [3:0] R0,
  input  [3:0] R1,
  input  [3:0] RW,
  input  clock,
  input  reset,
  input  \operação ,
  output [31:0] R0_D,
  output [31:0] R1_D
);

  wire demultiplexer_1_out0, demultiplexer_1_out1, demultiplexer_1_out2, demultiplexer_1_out3,
       demultiplexer_1_out4, demultiplexer_1_out5, demultiplexer_1_out6, demultiplexer_1_out7,
       demultiplexer_1_out8, demultiplexer_1_out9, demultiplexer_1_out10, demultiplexer_1_out11,
       demultiplexer_1_out12, demultiplexer_1_out13, demultiplexer_1_out14, demultiplexer_1_out15;
  wire [31:0] register_1_q, register_2_q, register_3_q, register_4_q, register_5_q, register_6_q,
       register_7_q, register_8_q, register_9_q, register_10_q, register_11_q, register_12_q, register_13_q,
       register_14_q, register_15_q, register_16_q;

  Demultiplexer #(.select(4), .enable("false")) demultiplexer_1 (
    .out0(demultiplexer_1_out0), .out1(demultiplexer_1_out1), .out2(demultiplexer_1_out2),
    .out3(demultiplexer_1_out3), .out4(demultiplexer_1_out4), .out5(demultiplexer_1_out5),
    .out6(demultiplexer_1_out6), .out7(demultiplexer_1_out7), .out8(demultiplexer_1_out8),
    .out9(demultiplexer_1_out9), .out10(demultiplexer_1_out10), .out11(demultiplexer_1_out11),
    .out12(demultiplexer_1_out12), .out13(demultiplexer_1_out13), .out14(demultiplexer_1_out14),
    .out15(demultiplexer_1_out15), .in(\operação ), .sel(RW));
  Register #(.width(32)) register_1 (
    .D(DATA_WRITE), .en(demultiplexer_1_out0), .Q(register_1_q), .clk(clock), .clr(reset));
  Register #(.width(32)) register_2 (
    .D(DATA_WRITE), .en(demultiplexer_1_out1), .Q(register_2_q), .clk(clock), .clr(reset));
  Register #(.width(32)) register_3 (
    .D(DATA_WRITE), .en(demultiplexer_1_out2), .Q(register_3_q), .clk(clock), .clr(reset));
  Register #(.width(32)) register_4 (
    .D(DATA_WRITE), .en(demultiplexer_1_out3), .Q(register_4_q), .clk(clock), .clr(reset));
  Register #(.width(32)) register_5 (
    .D(DATA_WRITE), .en(demultiplexer_1_out4), .Q(register_5_q), .clk(clock), .clr(reset));
  Register #(.width(32)) register_6 (
    .D(DATA_WRITE), .en(demultiplexer_1_out5), .Q(register_6_q), .clk(clock), .clr(reset));
  Register #(.width(32)) register_7 (
    .D(DATA_WRITE), .en(demultiplexer_1_out6), .Q(register_7_q), .clk(clock), .clr(reset));
  Register #(.width(32)) register_8 (
    .D(DATA_WRITE), .en(demultiplexer_1_out7), .Q(register_8_q), .clk(clock), .clr(reset));
  Register #(.width(32)) register_9 (
    .D(DATA_WRITE), .en(demultiplexer_1_out8), .Q(register_9_q), .clk(clock), .clr(reset));
  Register #(.width(32)) register_10 (
    .D(DATA_WRITE), .en(demultiplexer_1_out9), .Q(register_10_q), .clk(clock), .clr(reset));
  Register #(.width(32)) register_11 (
    .D(DATA_WRITE), .en(demultiplexer_1_out10), .Q(register_11_q), .clk(clock), .clr(reset));
  Register #(.width(32)) register_12 (
    .D(DATA_WRITE), .en(demultiplexer_1_out11), .Q(register_12_q), .clk(clock), .clr(reset));
  Register #(.width(32)) register_13 (
    .D(DATA_WRITE), .en(demultiplexer_1_out12), .Q(register_13_q), .clk(clock), .clr(reset));
  Register #(.width(32)) register_14 (
    .D(DATA_WRITE), .en(demultiplexer_1_out13), .Q(register_14_q), .clk(clock), .clr(reset));
  Register #(.width(32)) register_15 (
    .D(DATA_WRITE), .en(demultiplexer_1_out14), .Q(register_15_q), .clk(clock), .clr(reset));
  Register #(.width(32)) register_16 (
    .D(DATA_WRITE), .en(demultiplexer_1_out15), .Q(register_16_q), .clk(clock), .clr(reset));
  Multiplexer #(.select(4), .width(32), .enable("false")) multiplexer_1 (
    .in0(register_1_q), .in1(register_2_q), .in2(register_3_q), .in3(register_4_q), .in4(register_5_q),
    .in5(register_6_q), .in6(register_7_q), .in7(register_8_q), .in8(register_9_q), .in9(register_10_q),
    .in10(register_11_q), .in11(register_12_q), .in12(register_13_q), .in13(register_14_q),
    .in14(register_15_q), .in15(register_16_q), .out(R0_D), .sel(R0));
  Multiplexer #(.select(4), .width(32), .enable("false")) multiplexer_2 (
    .in0(register_1_q), .in1(register_2_q), .in2(register_3_q), .in3(register_4_q), .in4(register_5_q),
    .in5(register_6_q), .in6(register_7_q), .in7(register_8_q), .in8(register_9_q), .in9(register_10_q),
    .in10(register_11_q), .in11(register_12_q), .in12(register_13_q), .in13(register_14_q),
    .in14(register_15_q), .in15(register_16_q), .out(R1_D), .sel(R1));
endmodule

module UC (
  input  E0,
  input  E1,
  input  E2,
  input  E3,
  output write_reg,
  output branch,
  output read_mem,
  output write_mem,
  output jump,
  output imediato,
  output [3:0] out_11
);

  wire and_1_out, and_2_out, and_3_out, and_4_out, and_5_out, and_6_out, and_8_out, and_9_out, and_11_out,
       and_12_out, not_1_out, not_2_out, not_3_out, not_4_out, not_5_out, not_6_out, not_7_out, not_8_out,
       not_9_out, not_10_out, not_11_out;

  not not_1 (not_1_out, E0);
  and and_1 (and_1_out, not_1_out, not_2_out);
  not not_2 (not_2_out, E1);
  not not_3 (not_3_out, E0);
  not not_4 (not_4_out, E2);
  and and_2 (and_2_out, not_3_out, not_4_out, not_5_out);
  not not_5 (not_5_out, E3);
  not not_6 (not_6_out, E1);
  and and_3 (and_3_out, not_6_out, E3);
  and and_4 (and_4_out, E2, E3);
  and and_5 (and_5_out, E1, E2, not_7_out);
  not not_7 (not_7_out, E3);
  and and_6 (and_6_out, E0, E1);
  and and_7 (read_mem, E0, E3);
  and and_8 (and_8_out, E0, not_8_out);
  not not_8 (not_8_out, E3);
  and and_9 (and_9_out, E0, E1);
  not not_9 (not_9_out, E2);
  and and_10 (jump, E1, not_9_out, E3);
  and and_11 (and_11_out, E2, E3);
  and and_12 (and_12_out, E1, not_10_out, not_11_out);
  not not_10 (not_10_out, E2);
  not not_11 (not_11_out, E3);
  or or_1 (write_reg, and_1_out, and_2_out, and_3_out, and_4_out);
  or or_2 (branch, and_5_out, and_6_out);
  or or_3 (write_mem, and_8_out, and_9_out);
  or or_4 (imediato, and_11_out, and_12_out);

  assign out_11 = {E0, E1, E2, E3};
endmodule

module memoria_de_dados (
  input  [7:0] Adress,
  input  LW,
  input  SW,
  input  [31:0] in_4,
  input  CLK,
  input  RESET,
  output [31:0] out_7
);

  wire clk_t;

  and and_1 (clk_t, SW, CLK);
  RAM #(.dataWidth(32), .bus("separate")) ram_1 (
    .addr(Adress), .din(in_4), .data(out_7), .str(SW), .clk(CLK), .ld(LW), .clr(RESET));  // open: sel

  // Other names for the same wires on the sheet: RST = RESET
endmodule
